// Logisim project ALU.circ as structural Verilog: 1 circuit, main circuit ALU
module ALU (
  input  [31:0] A,
  input  [31:0] B,
  input  [4:0] Shift,
  input  [3:0] Codop,
  input  CarryIn,
  output [31:0] S,
  output [3:0] Flags
);

  wire and_1_out, bitselector_1_out, bitselector_2_out, bitselector_5_out, bitselector_6_out,
       bitselector_7_out, bitselector_8_out, bitselector_9_out, bitselector_10_out, bitselector_11_out, C1,
       C2, C5, comparator_1_eq, comparator_2_eq, comparator_3_eq, comparator_4_eq, leftshiftL, leftshiftR,
       not_1_out, not_6_out, subtractor_2_bout, xor_1_out, xor_2_out;
  wire [4:0] subtractor_4_out, subtractor_5_out;
  wire [31:0] AandB, AfoisB, AorB, AplusB, AplusBplusCIn, ASR, AxorB, BandNotA, BmoinsA, BmoinsAplusCInBarre,
       C4, LSL, LSR, not_3_out, not_4_out, notA, rotR, zero, ZeromoinsA;

  assign AandB = A & B;  // AND_Gate AandB, 32 bits wide
  not not_1 (not_1_out, CarryIn);
  assign AxorB = A ^ B;  // XOR_Gate AxorB, 32 bits wide
  Adder #(.width(32)) adder_1 (.a(A), .b(B), .out(AplusB), .cout(C1));  // open: cin
  Subtractor #(.width(32)) subtractor_1 (.a(B), .b(A), .out(BmoinsA), .bout(C2));  // open: bin
  Adder #(.width(32)) adder_2 (.a(A), .b(B), .out(AplusBplusCIn), .cin(CarryIn));  // open: cout
  Adder #(.width(32)) adder_3 ();  // open: a, b, out, cin, cout
  Subtractor #(.width(32)) subtractor_2 (
    .a(B), .b(A), .out(BmoinsAplusCInBarre), .bin(not_1_out), .bout(subtractor_2_bout));
  not not_2 (C5, subtractor_2_bout);
  Subtractor #(.width(32)) subtractor_3 (.a({32{1'b0}}), .b(A), .out(ZeromoinsA));  // open: bin, bout
  Multiplier #(.width(32)) multiplier_1 (.a(A), .b(B), .out(AfoisB), .cout(C4));  // open: cin
  assign not_3_out = ~A;  // NOT_Gate not_3, 32 bits wide
  assign zero = A & not_3_out;  // AND_Gate ZERO, 32 bits wide
  assign not_4_out = ~A;  // NOT_Gate not_4, 32 bits wide
  assign BandNotA = not_4_out & B;  // AND_Gate BandNotA, 32 bits wide
  assign notA = ~A;  // NOT_Gate not_5, 32 bits wide
  assign AorB = A | B;  // OR_Gate AorB, 32 bits wide
  Multiplexer #(.select(4), .width(32)) multiplexer_1 (
    .in0(AandB), .in1(AxorB), .in2(LSL), .in3(LSR), .in4(ASR), .in5(AplusBplusCIn),
    .in6(BmoinsAplusCInBarre), .in7(rotR), .in8(AandB), .in9(ZeromoinsA), .in10(BmoinsA), .in11(AplusB),
    .in12(AorB), .in13(AfoisB), .in14(BandNotA), .in15(notA), .out(S), .sel(Codop));
  Shifter #(.width(32)) shifter_1 (.in(B), .\dist (Shift), .out(LSL));
  Shifter #(.shift("lr"), .width(32)) shifter_2 (.in(B), .\dist (Shift), .out(LSR));
  Shifter #(.shift("ar"), .width(32)) shifter_3 (.in(B), .\dist (Shift), .out(ASR));
  Shifter #(.shift("rr"), .width(32)) shifter_4 (.in(B), .\dist (Shift), .out(rotR));
  BitSelector #(.width(32)) bitselector_1 (.in(B), .out(bitselector_1_out), .sel({5{1'b1}}));
  BitSelector #(.width(32)) bitselector_2 (.in(C4), .out(bitselector_2_out), .sel({5{1'b0}}));
  Subtractor #(.width(5)) subtractor_4 (.a({5{1'b0}}), .b(Shift), .out(subtractor_4_out));  // open: bin, bout
  Subtractor #(.width(5)) subtractor_5 (.a(Shift), .b(5'b00001), .out(subtractor_5_out));  // open: bin, bout
  BitSelector #(.width(32)) bitselector_3 (.in(B), .out(leftshiftL), .sel(subtractor_4_out));
  BitSelector #(.width(32)) bitselector_4 (.in(B), .out(leftshiftR), .sel(subtractor_5_out));
  BitSelector #(.width(32)) bitselector_5 (.in(S), .out(bitselector_5_out), .sel({5{1'b1}}));
  BitSelector #(.width(32)) bitselector_6 (.in(AandB), .out(bitselector_6_out), .sel({5{1'b1}}));
  BitSelector #(.width(32)) bitselector_7 (.in(BmoinsA), .out(bitselector_7_out), .sel({5{1'b1}}));
  BitSelector #(.width(32)) bitselector_8 (.in(AplusB), .out(bitselector_8_out), .sel({5{1'b1}}));
  Multiplexer #(.select(4)) multiplexer_2 (
    .in0(1'b0), .in1(1'b0), .in2(leftshiftL), .in3(leftshiftR), .in4(leftshiftR), .in5(C1), .in6(C2),
    .in7(bitselector_1_out), .in8(1'b0), .in9(1'b0), .in10(C5), .in11(C1), .in12(1'b0),
    .in13(bitselector_2_out), .in14(1'b0), .in15(1'b0), .out(Flags[1]), .sel(Codop));
  Multiplexer #(.select(4)) multiplexer_3 (
    .in0(bitselector_5_out), .in1(bitselector_5_out), .in2(bitselector_5_out), .in3(bitselector_5_out),
    .in4(bitselector_5_out), .in5(bitselector_5_out), .in6(bitselector_5_out), .in7(bitselector_5_out),
    .in8(bitselector_6_out), .in9(bitselector_5_out), .in10(bitselector_7_out), .in11(bitselector_8_out),
    .in12(bitselector_5_out), .in13(bitselector_5_out), .in14(bitselector_5_out), .in15(bitselector_5_out),
    .out(Flags[3]), .sel(Codop));
  BitSelector #(.width(32)) bitselector_9 (.in(A), .out(bitselector_9_out), .sel({5{1'b1}}));
  BitSelector #(.width(32)) bitselector_10 (.in(B), .out(bitselector_10_out), .sel({5{1'b1}}));
  BitSelector #(.width(32)) bitselector_11 (.in(S), .out(bitselector_11_out), .sel({5{1'b1}}));
  xor xor_1 (xor_1_out, bitselector_9_out, bitselector_10_out);
  xor xor_2 (xor_2_out, bitselector_10_out, bitselector_11_out);
  and and_1 (and_1_out, xor_1_out, xor_2_out);
  Comparator #(.mode("unsigned"), .width(32)) comparator_1 (
    .a(S), .b({32{1'b0}}), .eq(comparator_1_eq));  // open: gt, lt
  Comparator #(.mode("unsigned"), .width(32)) comparator_2 (
    .a(AandB), .b({32{1'b0}}), .eq(comparator_2_eq));  // open: gt, lt
  Comparator #(.mode("unsigned"), .width(32)) comparator_3 (
    .a(BmoinsA), .b({32{1'b0}}), .eq(comparator_3_eq));  // open: gt, lt
  Comparator #(.mode("unsigned"), .width(32)) comparator_4 (
    .a(AplusB), .b({32{1'b0}}), .eq(comparator_4_eq));  // open: gt, lt
  not not_6 (not_6_out, and_1_out);
  Multiplexer #(.select(4)) multiplexer_4 (
    .in0(comparator_1_eq), .in1(comparator_1_eq), .in2(comparator_1_eq), .in3(comparator_1_eq),
    .in4(comparator_1_eq), .in5(comparator_1_eq), .in6(comparator_1_eq), .in7(comparator_1_eq),
    .in8(comparator_2_eq), .in9(comparator_1_eq), .in10(comparator_3_eq), .in11(comparator_4_eq),
    .in12(comparator_1_eq), .in13(comparator_1_eq), .in14(comparator_1_eq), .in15(comparator_1_eq),
    .out(Flags[2]), .sel(Codop));
  Multiplexer #(.select(4)) multiplexer_5 (
    .in0(1'b0), .in1(1'b0), .in2(1'b0), .in3(1'b0), .in4(1'b0), .in5(and_1_out), .in6(and_1_out), .in7(1'b0),
    .in8(1'b0), .in9(1'b0), .in10(and_1_out), .in11(not_6_out), .in12(1'b0), .in13(1'b0), .in14(1'b0),
    .in15(1'b0), .out(Flags[0]), .sel(Codop));

  // Other names for the same wires on the sheet: CIn = CarryIn; V = Flags[0]; C = Flags[1]; Z = Flags[2];
  //   N = Flags[3]

  // Notes on the sheet:
  //   Note: for ROR, C = N
  //   Note 2: assume that shift > 0 for LSL and LSR
endmodule
