// Logisim project BancDeRegistres.circ as structural Verilog: 1 circuit, main circuit BancRegistre
module BancRegistre (
  input  [2:0] RegA,
  input  [2:0] RegB,
  input  [31:0] DataIn,
  input  [2:0] RegDest,
  input  Clk,
  input  Reset,
  output [31:0] AOut,
  output [31:0] BOut,
  output [31:0] R0,
  output [31:0] R1,
  output [31:0] R2,
  output [31:0] R3,
  output [31:0] R4,
  output [31:0] R5,
  output [31:0] R6,
  output [31:0] R7
);

  wire SD1, SD2, SD3, SD4, SD5, SD6, SD7, SD8;

  Register #(.width(32)) register_1 (.D(DataIn), .en(SD1), .clk(Clk), .Q(R0), .clr(Reset));
  Register #(.width(32)) register_2 (.D(DataIn), .en(SD2), .clk(Clk), .Q(R1), .clr(Reset));
  Register #(.width(32)) register_3 (.D(DataIn), .en(SD3), .clk(Clk), .Q(R2), .clr(Reset));
  Register #(.width(32)) register_4 (.D(DataIn), .en(SD4), .clk(Clk), .Q(R3), .clr(Reset));
  Register #(.width(32)) register_5 (.D(DataIn), .en(SD5), .clk(Clk), .Q(R4), .clr(Reset));
  Register #(.width(32)) register_6 (.D(DataIn), .en(SD6), .clk(Clk), .Q(R5), .clr(Reset));
  Register #(.width(32)) register_7 (.D(DataIn), .en(SD7), .clk(Clk), .Q(R6), .clr(Reset));
  Register #(.width(32)) register_8 (.D(DataIn), .en(SD8), .clk(Clk), .Q(R7), .clr(Reset));
  Decoder #(.enable("false"), .select(3)) decoder_1 (
    .out0(SD1), .out1(SD2), .out2(SD3), .out3(SD4), .out4(SD5), .out5(SD6), .out6(SD7), .out7(SD8),
    .sel(RegDest));
  Multiplexer #(.select(3), .width(32)) multiplexer_1 (
    .in0(R0), .in1(R1), .in2(R2), .in3(R3), .in4(R4), .in5(R5), .in6(R6), .in7(R7), .out(AOut), .sel(RegA));
  Multiplexer #(.select(3), .width(32)) multiplexer_2 (
    .in0(R0), .in1(R1), .in2(R2), .in3(R3), .in4(R4), .in5(R5), .in6(R6), .in7(R7), .out(BOut), .sel(RegB));

  // Other names for the same wires on the sheet: DIn[31:0] = DataIn; RegD[2:0] = RegDest; SM1[31:0] = R0;
  //   SM2[31:0] = R1; SM3[31:0] = R2; SM4[31:0] = R3; SM5[31:0] = R4; SM6[31:0] = R5; SM7[31:0] = R6; SM8[31:0] = R7
endmodule
