// Logisim project Ctl_Conditional.circ as structural Verilog: 1 circuit, main circuit Conditional
module Conditional (
  input  Enable,
  input  [15:0] Instruction,
  input  Z,
  input  C,
  input  N,
  input  V,
  output [10:0] Offset,
  output Verified
);

  wire CBarre, CBarreOuZ, CEtZBarre, NBarre, NDifferentDeV, NEgaleAV, VBarre, Verified_t, ZBarre,
       ZBarreEtNEgaleAV, ZOuNDifferentDeV;
  wire [10:0] imm8Ex;

  not not_1 (ZBarre, Z);
  not not_2 (CBarre, C);
  not not_3 (NBarre, N);
  not not_4 (VBarre, V);
  and and_1 (CEtZBarre, C, ZBarre);
  or or_1 (CBarreOuZ, CBarre, Z);
  Comparator #(.width(1)) comparator_1 (.a(N), .b(V), .eq(NEgaleAV));  // open: gt, lt
  not not_5 (NDifferentDeV, NEgaleAV);
  and and_2 (ZBarreEtNEgaleAV, ZBarre, NEgaleAV);
  or or_2 (ZOuNDifferentDeV, Z, NDifferentDeV);
  assign imm8Ex = {{3{Instruction[7]}}, Instruction[7:0]};  // Bit_Extender bit_extender_1
  Multiplexer #(.width(11)) multiplexer_1 (.in0(Instruction[10:0]), .in1(imm8Ex), .out(Offset), .sel(Instruction[12]));
  Multiplexer #(.select(4)) multiplexer_2 (
    .in0(Z), .in1(ZBarre), .in2(C), .in3(CBarre), .in4(N), .in5(NBarre), .in6(V), .in7(VBarre),
    .in8(CEtZBarre), .in9(CBarreOuZ), .in10(NEgaleAV), .in11(NDifferentDeV), .in12(ZBarreEtNEgaleAV),
    .in13(ZOuNDifferentDeV), .in14(1'b1), .in15(1'b0), .out(Verified_t), .sel(Instruction[11:8]));
  and and_3 (Verified, Verified_t, Enable);

  // Other names for the same wires on the sheet: imm8[7:0] = Instruction[7:0]; imm11[10:0] = Instruction[10:0];
  //   cond[3:0] = Instruction[11:8]; deux[4:0] = Instruction[15:11]; Bit12 = Instruction[12];
  //   un[3:0] = Instruction[15:12]
endmodule
