// Logisim project Ctl_Load_Store.circ as structural Verilog: 1 circuit, main circuit Load_Store
module Load_Store (
  input  [15:0] Instruction,
  input  Enable,
  input  Clk,
  input  Reset,
  input  [31:0] Stack_Pointer,
  output Store,
  output Load,
  output PC_Hold,
  output [2:0] Rmd,
  output [31:0] RAM_Addr
);

  wire and_1_out, L, not_1_out, PC, S;
  wire [2:0] E3;
  wire [31:0] E32, Imm32, RAM;

  assign E32 = {{31{1'b0}}, Enable};  // Bit_Extender bit_extender_1
  assign E3 = {{2{1'b0}}, Enable};  // Bit_Extender bit_extender_2
  assign Imm32 = {{24{Instruction[7]}}, Instruction[7:0]};  // Bit_Extender bit_extender_3
  Adder #(.width(32)) adder_1 (.a(Imm32), .b(Stack_Pointer), .out(RAM));  // open: cin, cout
  Comparator #(.width(1)) comparator_1 (.a(Instruction[11]), .b(1'b0), .gt(L), .eq(S));  // open: lt
  not not_1 (not_1_out, PC);
  D_Flip_Flop d_ff_1 (.D(and_1_out), .clk(Clk), .Q(PC), .reset(Reset));  // open: Qn, preset
  and and_1 (and_1_out, not_1_out, L);
  and and_2 (Store, S, Enable);
  and and_3 (Load, L, Enable);
  and and_4 (PC_Hold, PC, Enable);
  assign Rmd = Instruction[10:8] & E3;  // AND_Gate and_5, 3 bits wide
  assign RAM_Addr = RAM & E32;  // AND_Gate and_6, 32 bits wide

  // Other names for the same wires on the sheet: E = Enable; Imm8[7:0] = Instruction[7:0];
  //   Rt[2:0] = Instruction[10:8]; LorS = Instruction[11]; Rst = Reset; SP[31:0] = Stack_Pointer

  // Notes on the sheet:
  //   Instruction: pull=down
  //   Delay load and hold PC for 1 cycle for the RAM to send out requested data 
endmodule
