// Logisim project Ctl_SP_Address.circ as structural Verilog: 1 circuit, main circuit SP_Address
module SP_Address (
  input  [31:0] Stack_Pointer,
  input  [15:0] Instruction,
  input  in_3,
  output [31:0] New_Stack_Pointer,
  output Write_Enable
);

  wire SeptBits;
  wire [6:0] bitselector_2_out;
  wire [31:0] adder_1_out, bit_extender_2_out, imm7, multiplexer_1_out, subtractor_1_out;

  BitSelector #(.width(16)) bitselector_1 (.in(Instruction), .out(SeptBits), .sel(4'b0111));
  BitSelector #(.group(7), .width(16)) bitselector_2 (.in(Instruction), .out(bitselector_2_out), .sel(2'b00));
  assign imm7 = {{25{bitselector_2_out[6]}}, bitselector_2_out};  // Bit_Extender bit_extender_1
  Adder #(.width(32)) adder_1 (.a(Stack_Pointer), .b(imm7), .out(adder_1_out));  // open: cin, cout
  Subtractor #(.width(32)) subtractor_1 (.a(Stack_Pointer), .b(imm7), .out(subtractor_1_out));  // open: bin, bout
  Multiplexer #(.width(32)) multiplexer_1 (
    .in0(adder_1_out), .in1(subtractor_1_out), .out(multiplexer_1_out), .sel(SeptBits));
  assign bit_extender_2_out = {{31{in_3}}, in_3};  // Bit_Extender bit_extender_2
  assign New_Stack_Pointer = multiplexer_1_out & bit_extender_2_out;  // AND_Gate and_1, 32 bits wide

  assign Write_Enable = in_3;

  // Other names for the same wires on the sheet: enable = in_3

  // Notes on the sheet:
  //   Pull output low on Enable = 0
endmodule
